// Logisim project 8_BIT_2.circ as structural Verilog: 18 circuits, main circuit CPU
module ALU (
  input  [7:0] DATA_A,
  input  [7:0] DATA_B,
  input  [2:0] MODE,
  output [7:0] RESULT,
  output FLAG_Z,
  output FLAG_N,
  output FLAG_C,
  output FLAG_V
);

  wire add_8bit_1_c7_out, u2_converter_1_const_1;
  wire [7:0] add_8bit_1_sum_out, logic_1_out_and, logic_1_out_not, logic_1_out_or, logic_1_out_xor,
       pin_test_1_out_data, pin_test_2_out_data, pin_test_3_out_data, SHF_RIGHT_shlr_out,
       u2_converter_1_u2_out;

  PIN_TEST pin_test_1 (.IN_DATA(DATA_A), .OUT_DATA(pin_test_1_out_data));
  PIN_TEST pin_test_2 (.IN_DATA(DATA_B), .OUT_DATA(pin_test_2_out_data));
  U2_CONVERTER u2_converter_1 (
    .DATA_IN(pin_test_2_out_data), .SUB_OR_ADD(MODE[0]), .U2_OUT(u2_converter_1_u2_out),
    .CONST_1(u2_converter_1_const_1));
  LOGIC logic_1 (
    .DATA_A(pin_test_1_out_data), .DATA_B(pin_test_2_out_data), .OUT_AND(logic_1_out_and),
    .OUT_OR(logic_1_out_or), .OUT_XOR(logic_1_out_xor), .OUT_NOT(logic_1_out_not));
  SHIFT_RIGHT SHF_RIGHT (.SHLR_IN(pin_test_1_out_data), .SHLR_OUT(SHF_RIGHT_shlr_out));
  ADD_8BIT add_8bit_1 (
    .B(pin_test_1_out_data), .A(u2_converter_1_u2_out), .CIN(u2_converter_1_const_1),
    .SUM_OUT(add_8bit_1_sum_out), .CARRY(FLAG_C), .C7_OUT(add_8bit_1_c7_out));
  PIN_TEST pin_test_3 (.IN_DATA(add_8bit_1_sum_out), .OUT_DATA(pin_test_3_out_data));
  xor xor_1 (FLAG_V, FLAG_C, add_8bit_1_c7_out);
  Multiplexer #(.select(3), .width(8)) multiplexer_1 (
    .in0(pin_test_3_out_data), .in1(pin_test_3_out_data), .in2(logic_1_out_and), .in3(logic_1_out_or),
    .in4(logic_1_out_xor), .in5(logic_1_out_not), .in6(SHF_RIGHT_shlr_out), .in7(pin_test_2_out_data),
    .out(RESULT), .sel(MODE));
  Z_FLAG FLAGS (.DATA_IN(RESULT), .FLAG_Z(FLAG_Z), .FLAG_N(FLAG_N));

  // Other names for the same wires on the sheet: C_FLAG = FLAG_C; SUB_ON = MODE[0]; V_FLAG = FLAG_V
endmodule

module PIN_TEST (
  input  [7:0] IN_DATA,
  output [7:0] OUT_DATA
);

  wire n7_segment_display_1_p1, n7_segment_display_2_p1, n7_segment_display_3_p1;

  // _7_Segment_Display 7_segment_display_1: pin names not known; wires that end beside it: n7_segment_display_1_p1, n7_segment_display_1_p1
  // BCD_to_7_Segment_decoder bcd_to_7_segment_decoder_1: pin names not known
  // Binary_to_BCD_converter #(.binvalue(8)) binary_to_bcd_converter_1: pin names not known; wires that end beside it: IN_DATA
  // _7_Segment_Display 7_segment_display_2: pin names not known; wires that end beside it: n7_segment_display_2_p1, n7_segment_display_2_p1
  // _7_Segment_Display 7_segment_display_3: pin names not known; wires that end beside it: n7_segment_display_3_p1, n7_segment_display_3_p1
  // BCD_to_7_Segment_decoder bcd_to_7_segment_decoder_2: pin names not known
  // BCD_to_7_Segment_decoder bcd_to_7_segment_decoder_3: pin names not known

  assign OUT_DATA = IN_DATA;
endmodule

module ADD_1BIT (
  input  A,
  input  B,
  input  CIN,
  output SUM,
  output COUT
);

  wire and_1_out, and_2_out, and_3_out;

  xor xor_1 (SUM, A, B, CIN);
  and and_1 (and_1_out, A, B);
  and and_2 (and_2_out, A, CIN);
  and and_3 (and_3_out, CIN, B);
  or or_1 (COUT, and_1_out, and_2_out, and_3_out);
endmodule

module ADD_8BIT (
  input  [7:0] B,
  input  [7:0] A,
  input  CIN,
  output [7:0] SUM_OUT,
  output CARRY,
  output C7_OUT
);

  wire add_1bit_1_cout, add_1bit_2_cout, add_1bit_3_cout, add_1bit_4_cout, add_1bit_5_cout, WIRE_C;

  ADD_1BIT add_1bit_1 (.A(A[0]), .B(B[0]), .CIN(CIN), .SUM(SUM_OUT[0]), .COUT(add_1bit_1_cout));
  ADD_1BIT add_1bit_2 (.A(A[4]), .B(B[4]), .CIN(WIRE_C), .SUM(SUM_OUT[4]), .COUT(add_1bit_2_cout));
  ADD_1BIT add_1bit_3 (.A(A[1]), .B(B[1]), .CIN(add_1bit_1_cout), .SUM(SUM_OUT[1]), .COUT(add_1bit_3_cout));
  ADD_1BIT add_1bit_4 (.A(A[5]), .B(B[5]), .CIN(add_1bit_2_cout), .SUM(SUM_OUT[5]), .COUT(add_1bit_4_cout));
  ADD_1BIT add_1bit_5 (.A(A[2]), .B(B[2]), .CIN(add_1bit_3_cout), .SUM(SUM_OUT[2]), .COUT(add_1bit_5_cout));
  ADD_1BIT add_1bit_6 (.A(A[6]), .B(B[6]), .CIN(add_1bit_4_cout), .SUM(SUM_OUT[6]), .COUT(C7_OUT));
  ADD_1BIT add_1bit_7 (.A(A[3]), .B(B[3]), .CIN(add_1bit_5_cout), .SUM(SUM_OUT[3]), .COUT(WIRE_C));
  ADD_1BIT add_1bit_8 (.A(A[7]), .B(B[7]), .CIN(C7_OUT), .SUM(SUM_OUT[7]), .COUT(CARRY));

  // Other names for the same wires on the sheet: A1 = A[0]; A2 = A[1]; A3 = A[2]; A4 = A[3]; A5 = A[4]; A6 = A[5];
  //   A7 = A[6]; A8 = A[7]; B1 = B[0]; B2 = B[1]; B3 = B[2]; B4 = B[3]; B5 = B[4]; B6 = B[5]; B7 = B[6]; B8 = B[7];
  //   S1 = SUM_OUT[0]; S2 = SUM_OUT[1]; S3 = SUM_OUT[2]; S4 = SUM_OUT[3]; S5 = SUM_OUT[4]; S6 = SUM_OUT[5];
  //   S7 = SUM_OUT[6]; S8 = SUM_OUT[7]
endmodule

module LOGIC (
  input  [7:0] DATA_A,
  input  [7:0] DATA_B,
  output [7:0] OUT_AND,
  output [7:0] OUT_OR,
  output [7:0] OUT_XOR,
  output [7:0] OUT_NOT
);

  assign OUT_AND = DATA_A & DATA_B;  // AND_Gate and_1, 8 bits wide
  assign OUT_OR = DATA_A | DATA_B;  // OR_Gate or_1, 8 bits wide
  assign OUT_XOR = DATA_A ^ DATA_B;  // XOR_Gate xor_1, 8 bits wide
  assign OUT_NOT = ~DATA_A;  // NOT_Gate not_1, 8 bits wide
endmodule

module SHIFT_LEFT (
  input  [7:0] SHLF_IN,
  output [7:0] SHLF_OUT
);

  LED led_1 (.in(SHLF_IN[7]));
  LED led_2 (.in(SHLF_IN[6]));
  LED led_3 (.in(SHLF_IN[5]));
  LED led_4 (.in(SHLF_IN[4]));
  LED led_5 (.in(SHLF_IN[3]));
  LED led_6 (.in(SHLF_IN[2]));
  LED led_7 (.in(SHLF_IN[1]));
  LED led_8 (.in(SHLF_IN[0]));
  Pull_Resistor pull_resistor_1 (.node(SHLF_IN[7]));
  Pull_Resistor pull_resistor_2 (.node(SHLF_OUT[0]));
  LED led_9 (.in(SHLF_IN[6]));
  LED led_10 (.in(SHLF_IN[5]));
  LED led_11 (.in(SHLF_IN[4]));
  LED led_12 (.in(SHLF_IN[3]));
  LED led_13 (.in(SHLF_IN[2]));
  LED led_14 (.in(SHLF_IN[1]));
  LED led_15 (.in(SHLF_IN[0]));
  LED led_16 (.in(SHLF_OUT[0]));

  assign SHLF_OUT[7:1] = SHLF_IN[6:0];
endmodule

module SHIFT_RIGHT (
  input  [7:0] SHLR_IN,
  output [7:0] SHLR_OUT
);

  LED led_1 (.in(SHLR_IN[7]));
  LED led_2 (.in(SHLR_IN[6]));
  LED led_3 (.in(SHLR_IN[5]));
  LED led_4 (.in(SHLR_IN[4]));
  LED led_5 (.in(SHLR_IN[3]));
  LED led_6 (.in(SHLR_IN[2]));
  LED led_7 (.in(SHLR_IN[1]));
  LED led_8 (.in(SHLR_IN[0]));
  Pull_Resistor pull_resistor_1 (.node(SHLR_IN[0]));
  Pull_Resistor pull_resistor_2 (.node(SHLR_OUT[7]));
  LED led_9 (.in(SHLR_IN[6]));
  LED led_10 (.in(SHLR_IN[5]));
  LED led_11 (.in(SHLR_OUT[7]));
  LED led_12 (.in(SHLR_IN[7]));
  LED led_13 (.in(SHLR_IN[4]));
  LED led_14 (.in(SHLR_IN[3]));
  LED led_15 (.in(SHLR_IN[2]));
  LED led_16 (.in(SHLR_IN[1]));

  assign SHLR_OUT[6:0] = SHLR_IN[7:1];
endmodule

module U2_CONVERTER (
  input  [7:0] DATA_IN,
  input  SUB_OR_ADD,
  output [7:0] U2_OUT,
  output CONST_1
);

  wire [7:0] not_1_out;

  Multiplexer #(.width(8)) multiplexer_1 (.in0(DATA_IN), .in1(not_1_out), .out(U2_OUT), .sel(SUB_OR_ADD));
  assign not_1_out = ~DATA_IN;  // NOT_Gate not_1, 8 bits wide

  assign CONST_1 = SUB_OR_ADD;
endmodule

module Z_FLAG (
  input  [7:0] DATA_IN,
  output FLAG_Z,
  output FLAG_N
);

  nor nor_1 (FLAG_Z, DATA_IN[0], DATA_IN[1], DATA_IN[2], DATA_IN[3], DATA_IN[4], DATA_IN[5], DATA_IN[6], DATA_IN[7]);

  assign FLAG_N = DATA_IN[7];
endmodule

module REG_FILE (
  input  [7:0] DATA_IN,
  input  [3:0] READ_ADDR_A,
  input  ENABLE,
  input  [3:0] WRITE_ADDR,
  input  [3:0] READ_ADRR_B,
  input  CLOCK,
  output [7:0] OUTPUT_A,
  output [7:0] OUTPUT_B
);

  wire R0, R1, R2, R3, R4, R5, R6, R7, R8, R9, R10, R11, R12, R13, R14, R15;
  wire [7:0] R0_q, R1_q, R2_q, R3_q, R4_q, R5_q, R6_q, R7_q, R8_q, R9_q, R10_q, R11_q, R12_q, R13_q, R14_q,
       R15_q;

  Decoder #(.select(4)) decoder_1 (
    .out0(R0), .out1(R1), .out2(R2), .out3(R3), .out4(R4), .out5(R5), .out6(R6), .out7(R7), .out8(R8),
    .out9(R9), .out10(R10), .out11(R11), .out12(R12), .out13(R13), .out14(R14), .out15(R15),
    .sel(WRITE_ADDR), .en(ENABLE));
  Register u_R0 (.D(DATA_IN), .en(R0), .clk(CLOCK), .Q(R0_q));  // open: clr
  Register u_R1 (.D(DATA_IN), .en(R1), .clk(CLOCK), .Q(R1_q));  // open: clr
  Register u_R2 (.D(DATA_IN), .en(R2), .clk(CLOCK), .Q(R2_q));  // open: clr
  Register u_R3 (.D(DATA_IN), .en(R3), .clk(CLOCK), .Q(R3_q));  // open: clr
  Register u_R4 (.D(DATA_IN), .en(R4), .clk(CLOCK), .Q(R4_q));  // open: clr
  Register u_R5 (.D(DATA_IN), .en(R5), .clk(CLOCK), .Q(R5_q));  // open: clr
  Register u_R6 (.D(DATA_IN), .en(R6), .clk(CLOCK), .Q(R6_q));  // open: clr
  Register u_R7 (.D(DATA_IN), .en(R7), .clk(CLOCK), .Q(R7_q));  // open: clr
  Register u_R8 (.D(DATA_IN), .en(R8), .clk(CLOCK), .Q(R8_q));  // open: clr
  Register u_R9 (.D(DATA_IN), .en(R9), .clk(CLOCK), .Q(R9_q));  // open: clr
  Register u_R10 (.D(DATA_IN), .en(R10), .clk(CLOCK), .Q(R10_q));  // open: clr
  Register u_R11 (.D(DATA_IN), .en(R11), .clk(CLOCK), .Q(R11_q));  // open: clr
  Register u_R12 (.D(DATA_IN), .en(R12), .clk(CLOCK), .Q(R12_q));  // open: clr
  Register u_R13 (.D(DATA_IN), .en(R13), .clk(CLOCK), .Q(R13_q));  // open: clr
  Register u_R14 (.D(DATA_IN), .en(R14), .clk(CLOCK), .Q(R14_q));  // open: clr
  Register u_R15 (.D(DATA_IN), .en(R15), .clk(CLOCK), .Q(R15_q));  // open: clr
  Multiplexer #(.select(4), .width(8)) multiplexer_1 (
    .in0(R0_q), .in1(R1_q), .in2(R2_q), .in3(R3_q), .in4(R4_q), .in5(R5_q), .in6(R6_q), .in7(R7_q),
    .in8(R8_q), .in9(R9_q), .in10(R10_q), .in11(R11_q), .in12(R12_q), .in13(R13_q), .in14(R14_q),
    .in15(R15_q), .out(OUTPUT_A), .sel(READ_ADDR_A));
  Multiplexer #(.select(4), .width(8)) multiplexer_2 (
    .in0(R0_q), .in1(R1_q), .in2(R2_q), .in3(R3_q), .in4(R4_q), .in5(R5_q), .in6(R6_q), .in7(R7_q),
    .in8(R8_q), .in9(R9_q), .in10(R10_q), .in11(R11_q), .in12(R12_q), .in13(R13_q), .in14(R14_q),
    .in15(R15_q), .out(OUTPUT_B), .sel(READ_ADRR_B));

  // Other names for the same wires on the sheet: C = CLOCK
endmodule

module FLAG_REG (
  input  FLAG_Z,
  input  FLAG_N,
  input  FLAG_C,
  input  FLAG_V,
  input  Flag_Enable,
  input  C,
  output [3:0] FLAGS
);

  Register #(.width(4)) register_1 (
    .D({FLAG_V, FLAG_C, FLAG_N, FLAG_Z}), .en(Flag_Enable), .clk(C), .Q(FLAGS));  // open: clr
endmodule

module PC_COUNTER (
  input  [7:0] JUMP_ADR,
  input  PC_En,
  input  JUMP,
  input  clock,
  input  RESET,
  output [7:0] CURRENT_INSTRUCTION
);

  wire bcd_to_7_segment_decoder_2_p1, bcd_to_7_segment_decoder_3_p1, binary_to_bcd_converter_1_p2,
       pull_resistor_1_node;
  wire [7:0] add_8bit_1_sum_out, multiplexer_1_out;

  Multiplexer #(.width(8)) multiplexer_1 (
    .in0(add_8bit_1_sum_out), .in1(JUMP_ADR), .out(multiplexer_1_out), .sel(JUMP));
  Register register_1 (.D(multiplexer_1_out), .en(PC_En), .clk(clock), .Q(CURRENT_INSTRUCTION), .clr(RESET));
  Pull_Resistor pull_resistor_1 (.node(pull_resistor_1_node));
  _7_Segment_Display u_7_segment_display_1 ();  // open: g, f, a, b, e, d, c, dp
  // BCD_to_7_Segment_decoder bcd_to_7_segment_decoder_1: pin names not known
  _7_Segment_Display u_7_segment_display_2 ();  // open: g, f, a, b, e, d, c, dp
  // BCD_to_7_Segment_decoder bcd_to_7_segment_decoder_2: pin names not known; wires that end beside it: bcd_to_7_segment_decoder_2_p1
  // Binary_to_BCD_converter #(.binvalue(8)) binary_to_bcd_converter_1: pin names not known; wires that end beside it: CURRENT_INSTRUCTION, binary_to_bcd_converter_1_p2, binary_to_bcd_converter_1_p2, bcd_to_7_segment_decoder_2_p1
  _7_Segment_Display u_7_segment_display_3 ();  // open: g, f, a, b, e, d, c, dp
  // BCD_to_7_Segment_decoder bcd_to_7_segment_decoder_3: pin names not known; wires that end beside it: bcd_to_7_segment_decoder_3_p1, bcd_to_7_segment_decoder_3_p1
  ADD_8BIT add_8bit_1 (
    .B(CURRENT_INSTRUCTION), .A(8'h1), .CIN(pull_resistor_1_node), .SUM_OUT(add_8bit_1_sum_out));  // open: CARRY, C7_OUT
endmodule

module CONTROL_UNIT (
  input  [3:0] OPCODE,
  input  [3:0] FLAGS,
  output MEM_WE,
  output REG_WE,
  output FLAG_WE,
  output PC_JUMP,
  output PC_EN,
  output [2:0] ALU_OP,
  output [1:0] WB_SRC,
  output RAM_ADDR_SEL
);

  wire and_1_out, DEC_ADD, DEC_AND, DEC_BEQ, DEC_CMP, DEC_HALT, DEC_IND, DEC_JMP, DEC_LOAD, DEC_MOV, DEC_NOT,
       DEC_OR, DEC_STORE, DEC_STR, DEC_SUB, DEC_XOR, pull_resistor_1_node, pull_resistor_2_node,
       pull_resistor_3_node, pull_resistor_4_node, pull_resistor_5_node;

  Decoder #(.enable("false"), .select(4)) decoder_1 (
    .out0(DEC_ADD), .out1(DEC_SUB), .out2(DEC_AND), .out3(DEC_OR), .out4(DEC_XOR), .out5(DEC_NOT),
    .out6(DEC_MOV), .out7(DEC_CMP), .out8(DEC_LOAD), .out9(DEC_STORE), .out10(WB_SRC[1]), .out11(DEC_JMP),
    .out12(DEC_BEQ), .out13(DEC_STR), .out14(DEC_IND), .out15(DEC_HALT), .sel(OPCODE));
  Pull_Resistor pull_resistor_1 (.node(pull_resistor_1_node));
  Pull_Resistor pull_resistor_2 (.node(pull_resistor_2_node));
  or or_1 (ALU_OP[0], DEC_SUB, DEC_OR, DEC_NOT, DEC_CMP, DEC_MOV);
  or or_2 (ALU_OP[1], DEC_AND, DEC_OR, pull_resistor_1_node, DEC_MOV);
  or or_3 (ALU_OP[2], DEC_XOR, DEC_NOT, pull_resistor_2_node, DEC_MOV);
  Pull_Resistor pull_resistor_3 (.node(pull_resistor_3_node));
  Pull_Resistor pull_resistor_4 (.node(pull_resistor_4_node));
  Pull_Resistor pull_resistor_5 (.node(pull_resistor_5_node));
  and and_1 (and_1_out, DEC_BEQ, FLAGS[0]);
  not not_1 (PC_EN, DEC_HALT);
  or or_4 (MEM_WE, DEC_STORE, DEC_STR);
  or or_5 (PC_JUMP, DEC_JMP, and_1_out);
  or or_6 (WB_SRC[0], DEC_IND, DEC_LOAD);
  or or_7 (REG_WE, pull_resistor_3_node, DEC_ADD, DEC_SUB, DEC_AND, DEC_OR, DEC_XOR, DEC_NOT, DEC_MOV, DEC_LOAD, WB_SRC[1], DEC_IND);
  or or_8 (FLAG_WE, pull_resistor_4_node, DEC_ADD, DEC_SUB, DEC_AND, DEC_OR, DEC_XOR, DEC_NOT, DEC_CMP, pull_resistor_5_node);
  or or_9 (RAM_ADDR_SEL, DEC_STR, DEC_IND);

  // Other names for the same wires on the sheet: FLAG_Z = FLAGS[0]; FLAG_N = FLAGS[1]; FLAG_C = FLAGS[2];
  //   FLAG_V = FLAGS[3]; DEC_LDI = WB_SRC[1]
endmodule

module ROM_SPLITER (
  input  [15:0] ROM_IN,
  output [3:0] READ_ADDR_B,
  output [7:0] ADR,
  output [3:0] REG_INDEX,
  output [3:0] OPCODE
);


  assign ADR = ROM_IN[7:0];
  assign OPCODE = ROM_IN[15:12];
  assign READ_ADDR_B = ROM_IN[3:0];
  assign REG_INDEX = ROM_IN[11:8];
endmodule

module TTY_CONVERTER (
  input  [7:0] TTY_IN,
  output [6:0] TTY_OUT
);


  assign TTY_OUT = TTY_IN[6:0];
endmodule

module CPU (
);

  wire ACK, alu_1_flag_c, alu_1_flag_n, alu_1_flag_v, alu_1_flag_z, and_1_out, bcd_to_7_segment_decoder_3_p1,
       binary_to_bcd_converter_1_p2, binary_to_bcd_converter_1_p4, C, FLAG_EN, IS_KEYBOARD, MEM_WE, PC_EN,
       PC_JUMP, RAM_ADR_SEL, REG_WE, RESET, TTY_EN;
  wire [1:0] WB_SRC;
  wire [2:0] ALU_OP;
  wire [3:0] FLAGS, PAGE, READ_ADDR_B, REG_INDEX, rom_spliter_1_opcode;
  wire [6:0] keyboard_1_data, tty_converter_1_tty_out;
  wire [7:0] ADDRESS, ADRES_IO, ALU_RESULT, DISPLAY, dotmatrix_1_p1, dotmatrix_1_p2, KEYBOARD_OUT,
       multiplexer_1_out, pc_counter_1_current_instruction, ram_1_dout, RAM_OUT, reg_file_1_output_a,
       reg_file_1_output_b, TTY_IN;
  wire [15:0] rom_1_data;

  Clock clock_1 (.out(C));
  not not_1 (RESET, PC_EN);
  ROM #(.dataWidth(16)) rom_1 (.addr(pc_counter_1_current_instruction), .data(rom_1_data));
  PC_COUNTER pc_counter_1 (
    .JUMP_ADR(ADDRESS), .PC_En(PC_EN), .JUMP(PC_JUMP), .clock(C), .RESET(RESET),
    .CURRENT_INSTRUCTION(pc_counter_1_current_instruction));
  ROM_SPLITER rom_spliter_1 (
    .ROM_IN(rom_1_data), .READ_ADDR_B(READ_ADDR_B), .ADR(ADDRESS), .REG_INDEX(REG_INDEX),
    .OPCODE(rom_spliter_1_opcode));
  Multiplexer #(.select(2), .width(8)) multiplexer_1 (
    .in0(ALU_RESULT), .in1(RAM_OUT), .in2(ADDRESS), .out(multiplexer_1_out), .sel(WB_SRC));  // open: in3
  _7_Segment_Display u_7_segment_display_1 ();  // open: g, f, a, b, e, d, c, dp
  // BCD_to_7_Segment_decoder bcd_to_7_segment_decoder_1: pin names not known
  // Binary_to_BCD_converter #(.binvalue(8)) binary_to_bcd_converter_1: pin names not known; wires that end beside it: DISPLAY, binary_to_bcd_converter_1_p2, binary_to_bcd_converter_1_p2, binary_to_bcd_converter_1_p4
  Keyboard keyboard_1 (.re(and_1_out), .clr(ACK), .data(keyboard_1_data));  // open: clk, avail
  and and_1 (and_1_out, MEM_WE, IS_KEYBOARD);
  CONTROL_UNIT control_unit_1 (
    .OPCODE(rom_spliter_1_opcode), .FLAGS(FLAGS), .MEM_WE(MEM_WE), .REG_WE(REG_WE), .FLAG_WE(FLAG_EN),
    .PC_JUMP(PC_JUMP), .PC_EN(PC_EN), .ALU_OP(ALU_OP), .WB_SRC(WB_SRC), .RAM_ADDR_SEL(RAM_ADR_SEL));
  _7_Segment_Display u_7_segment_display_2 ();  // open: g, f, a, b, e, d, c, dp
  _7_Segment_Display u_7_segment_display_3 ();  // open: g, f, a, b, e, d, c, dp
  // BCD_to_7_Segment_decoder bcd_to_7_segment_decoder_2: pin names not known; wires that end beside it: binary_to_bcd_converter_1_p4
  // BCD_to_7_Segment_decoder bcd_to_7_segment_decoder_3: pin names not known; wires that end beside it: bcd_to_7_segment_decoder_3_p1, bcd_to_7_segment_decoder_3_p1
  TTY_CONVERTER tty_converter_1 (.TTY_IN(TTY_IN), .TTY_OUT(tty_converter_1_tty_out));
  assign KEYBOARD_OUT = {{1{keyboard_1_data[6]}}, keyboard_1_data};  // Bit_Extender bit_extender_1
  TTY tty_1 (.data(tty_converter_1_tty_out), .clk(C), .we(TTY_EN));  // open: clr
  REG_FILE reg_file_1 (
    .DATA_IN(multiplexer_1_out), .READ_ADDR_A(REG_INDEX), .ENABLE(REG_WE), .WRITE_ADDR(REG_INDEX),
    .READ_ADRR_B(READ_ADDR_B), .CLOCK(C), .OUTPUT_A(reg_file_1_output_a), .OUTPUT_B(reg_file_1_output_b));
  Multiplexer #(.width(8)) multiplexer_2 (.in0(ADDRESS), .in1(reg_file_1_output_b), .out(ADRES_IO), .sel(RAM_ADR_SEL));
  ALU alu_1 (
    .DATA_A(reg_file_1_output_a), .DATA_B(reg_file_1_output_b), .MODE(ALU_OP), .RESULT(ALU_RESULT),
    .FLAG_Z(alu_1_flag_z), .FLAG_N(alu_1_flag_n), .FLAG_C(alu_1_flag_c), .FLAG_V(alu_1_flag_v));
  RAM #(.addrWidth(12), .enables("line")) ram_1 (
    .addr({PAGE, ADRES_IO}), .we(MEM_WE), .clk(C), .din(reg_file_1_output_a), .dout(ram_1_dout));
  IO io_1 (
    .DATA(reg_file_1_output_a), .ADR(ADRES_IO), .MEM_WE(MEM_WE), .C(C), .RESET(RESET), .DISPLAY(DISPLAY),
    .TTY_IN(TTY_IN), .TTY_EN(TTY_EN), .IS_KEY(IS_KEYBOARD), .ACK(ACK), .PAGE(PAGE));
  // DotMatrix #(.inputtype("select"), .matrixcols(8), .matrixrows(8)) dotmatrix_1: pin names not known; wires that end beside it: dotmatrix_1_p1, dotmatrix_1_p2
  GPU_8X8_CONTROL gpu_8x8_control_1 (
    .DATA_IN(reg_file_1_output_a), .ADR(ADRES_IO), .BANK_ID(PAGE), .MEM_WE(MEM_WE), .COLUMNS(dotmatrix_1_p1),
    .ROWS(dotmatrix_1_p2));
  FLAG_REG flag_reg_1 (
    .FLAG_Z(alu_1_flag_z), .FLAG_N(alu_1_flag_n), .FLAG_C(alu_1_flag_c), .FLAG_V(alu_1_flag_v),
    .Flag_Enable(FLAG_EN), .C(C), .FLAGS(FLAGS));
  Multiplexer #(.width(8)) multiplexer_3 (.in0(ram_1_dout), .in1(KEYBOARD_OUT), .out(RAM_OUT), .sel(IS_KEYBOARD));

  // Notes on the sheet:
  //   contents of rom_1 (hex, n*v repeats v):
  //   affe a048 d00f a065 d00f a06c d00f a06c d00f a06f d00f a020 d00f a057 d00f a06f d00f a072 d00f a06c
  //   d00f a064 d00f a021 d00f f000
endmodule

module IO (
  input  [7:0] DATA,
  input  [7:0] ADR,
  input  MEM_WE,
  input  C,
  input  RESET,
  output [7:0] DISPLAY,
  output [7:0] TTY_IN,
  output TTY_EN,
  output IS_KEY,
  output ACK,
  output [3:0] PAGE
);

  wire and_1_out, and_4_out, comparator_1_eq, comparator_2_eq, comparator_4_eq;

  Comparator comparator_1 (.a(ADR), .b({8{1'b1}}), .eq(comparator_1_eq));  // open: gt, lt
  Comparator comparator_2 (.a(ADR), .b(8'hfe), .eq(comparator_2_eq));  // open: gt, lt
  Comparator comparator_3 (.a(ADR), .b(8'hfd), .eq(IS_KEY));  // open: gt, lt
  Comparator comparator_4 (.a(ADR), .b(8'hfc), .eq(comparator_4_eq));  // open: gt, lt
  and and_1 (and_1_out, comparator_1_eq, MEM_WE);
  and and_2 (TTY_EN, comparator_2_eq, MEM_WE);
  and and_3 (ACK, IS_KEY, MEM_WE);
  and and_4 (and_4_out, comparator_4_eq, MEM_WE);
  Register register_1 (.D(DATA), .en(and_1_out), .clk(C), .Q(DISPLAY), .clr(RESET));
  assign TTY_IN = TTY_EN ? DATA : 8'bz;  // Controlled_Buffer controlled_buffer_1
  Register #(.width(4)) BANK_REG (.D(DATA[3:0]), .en(and_4_out), .clk(C), .Q(PAGE), .clr(RESET));

  // Other names for the same wires on the sheet: R = RESET
endmodule

module GPU_8X8_CONTROL (
  input  [7:0] DATA_IN,
  input  [7:0] ADR,
  input  [3:0] BANK_ID,
  input  MEM_WE,
  output [7:0] COLUMNS,
  output [7:0] ROWS
);

  wire and_1_out, and_2_out, comparator_1_eq, not_1_out;

  Decoder #(.enable("false"), .select(3)) decoder_1 (
    .out0(ROWS[0]), .out1(ROWS[1]), .out2(ROWS[2]), .out3(ROWS[3]), .out4(ROWS[4]), .out5(ROWS[5]),
    .out6(ROWS[6]), .out7(ROWS[7]), .sel(ADR[2:0]));
  not not_1 (not_1_out, ADR[3]);
  and and_1 (and_1_out, not_1_out, ADR[4], ADR[5], ADR[6], ADR[7]);
  Comparator #(.width(4)) comparator_1 (.a(BANK_ID), .b(4'b0011), .eq(comparator_1_eq));  // open: gt, lt
  and and_2 (and_2_out, and_1_out, comparator_1_eq, MEM_WE);
  Pull_Resistor pull_resistor_1 (.node(COLUMNS));
  assign COLUMNS = and_2_out ? DATA_IN : 8'bz;  // Controlled_Buffer controlled_buffer_1
endmodule
